# Fritzing sketch divider (saved by Fritzing 0.9.2b)
breadboards: 1

parts:
  J1 = Basic Force Sensing Resistor (FSR) [package=THT]
  R1 = Resistor [tolerance=±5% resistance=250k package=THT]
  Part1 = Photon

nets:
  N1: J1.pin_0, Part1.3V3
  N2: J1.pin_1, R1.Pin_0, Part1.A2
  N3: R1.Pin_1, Part1.GND
