# Fritzing sketch neopixel (saved by Fritzing 0.9.2b)
breadboards: 1

parts:
  LED1 = Adafruit_FLORA_RGB_Smart_Pixel
  LED2 = Adafruit_FLORA_RGB_Smart_Pixel
  Part1 = Photon
  R1 = Resistor [tolerance=±5% resistance=500 package="2512 [SMD]"]

nets:
  N1: LED1.connector1, LED2.connector1, R1.Pin_1
  N2: LED1.connector2, Part1.D2
  GND: LED1.connector3, LED2.connector3
  N3: LED1.connector4, LED2.connector2
  N4: Part1.VIN, R1.Pin_0
