# Fritzing sketch outputs (saved by Fritzing 0.9.2b)
breadboards: 1

parts:
  Part1 = Photon
  PowerBoost_500C = PowerBoost 500 Charger
  Part3 = LilyPad Slide Switch
  LED1 = smd LED [color="Red (633nm)" package="0805 [SMD]"]
  M1 = DC Motor
  J1 = Piezo Speaker

nets:
  N1: Part1.VIN, PowerBoost_500C.5.0V
  N2: Part1.D0, LED1.anode
  N3: Part1.D1, M1.pin_1
  N4: Part1.D2, J1.pin1
  GND: PowerBoost_500C.GND, Part3.OFF, LED1.cathode, M1.pin_2, J1.pin2
  N5: PowerBoost_500C.ENABLE, Part3.ON

custom parts:
  PowerBoost 500 Charger: The PowerBoost 500C is a little DC/DC boost converter module that can be powered by any 3.7V LiIon/LiPoly battery, and convert the battery output to 5.2V DC for running your 5V projects. At its heart is a TPS61090 boost converter from TI. This boost converter chip has some really nice extras such as low battery detection, 2A internal switch, synchronous conversion, excellent efficiency, and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
