# Fritzing sketch pulldown (saved by Fritzing 0.9.2b)

parts:
  part = Photon
  part_2 = LilyPad Button Board
  R1 = Resistor [tolerance=±5% resistance=10k package="0603 [SMD]"]

nets:
  N1: part.GND, R1.Pin_1
  N2: part.VIN, part_2.-
  N3: part.D2, part_2.S, R1.Pin_0
