# Fritzing sketch transistor (saved by Fritzing 0.9.2b)

parts:
  Q1 = NPN-Transistor [package="TO92 [THT]"]
  Part1 = Photon
  LED1 = smd LED [color="Red (633nm)" package="1206 [SMD]"]
  LED2 = smd LED [color="Red (633nm)" package="1206 [SMD]"]
  LED3 = smd LED [color="Red (633nm)" package="1206 [SMD]"]
  LED4 = smd LED [color="Red (633nm)" package="1206 [SMD]"]
  R1 = Resistor [tolerance=±5% resistance=220 package="0603 [SMD]"]

nets:
  N1: Q1.E, LED1.anode
  N2: Q1.B, Part1.D7
  N3: Q1.C, Part1.VIN
  N4: Part1.GND, R1.Pin_0
  N5: LED1.cathode, LED2.anode
  N6: LED2.cathode, LED3.anode
  N7: LED3.cathode, LED4.anode
  N8: LED4.cathode, R1.Pin_1
